# Fritzing sketch config_BT2 (saved by Fritzing 0.9.10b)

parts:
  Part2 = Arduino Uno (Rev3)
  Part3 = Bluetooth HC-05 Macho

nets:
  N1: Part2.D12/MISO, Part3.RXD
  N2: Part2.D13/SCK, Part3.TXD
  GND: Part2.GND, Part3.GND
  N3: Part2.3V3, Part3.Key
  5V: Part2.5V, Part3.VCC
