# Fritzing sketch vmc_prefinal (saved by Fritzing 0.9.10b)
breadboards: 1

parts:
  Part4 = Arduino Uno (Rev3)
  A7 = DHT22 module
  A8 = DHT22 module
  A9 = DHT22 module
  Part5 = Bluetooth HC-05 Macho
  R3 = Resistor [tolerance=±5% resistance=1k package="2512 [SMD]"]
  F1 = Fan - 4 wire [package=THT]
  F2 = Fan - 4 wire [package=THT]
  U1 = 2-Channel 5v Relay Shield [package=relay-2ch5v10a]
  R5 = Resistor [tolerance=±5% resistance=2 package="0805 [SMD]"]
  R4 = Resistor [tolerance=±5% resistance=2 package="2512 [SMD]"]
  R6 = Resistor [tolerance=±5% resistance=2 package="0805 [SMD]"]
  R7 = Resistor [tolerance=±5% resistance=10k package="0805 [SMD]"]
  R8 = Resistor [tolerance=±5% resistance=10k package="0805 [SMD]"]

nets:
  N1: Part4.D8, U1.IN2
  N2: Part4.D9_PWM, R6.Pin_0
  N3: Part4.D10_PWM/SS, R5.Pin_0
  N4: Part4.D12/MISO, R3.Pin_0
  N5: Part4.D13/SCK, Part5.TXD
  GND: Part4.GND, A7.-, A8.-, A9.-, Part5.GND, F1.PWM, F2.PWM, U1.GND, R4.Pin_1, R7.Pin_1, R8.Pin_1
  N6: Part4.D2, R8.Pin_0
  N7: Part4.D3_PWM, R7.Pin_0
  N8: Part4.D4, A9.Out
  N9: Part4.D5_PWM, A7.Out
  N10: Part4.D6_PWM, A8.Out
  N11: Part4.D7, U1.IN1
  VCC: Part4.5V, A7.+, A8.+, A9.+, Part5.VCC, U1.VCC
  N12: Part5.RXD, R3.Pin_1, R4.Pin_0
  GND_2: F1.GND, F2.GND
  N13: F1.Power, U1.K1-In
  N14: F1.Tach, R5.Pin_1
  N15: F2.Power, U1.K2-In
  N16: F2.Tach, R6.Pin_1
  N17: U1.K1-Off, U1.K2-Off

notes:
  -3 sondes captes l'humidité
  -1 module BT reçoit des commandes et envoit des informations
  Résistances 2K et 1K entre le RXD et la carte
  - 2 Ventilateurs 12V DC PWM 4 fils
  R 2K sur le PWM
  R 10K sur le Sensor
  ON/OFF via double relay
  Alimentés par adaptateur 12V 2A
  5V
  GND
  12V +
  12V -
  PWM
  Sensor
  10K
  2K
  1K

custom parts:
  DHT22 module: DHT22 module. Pins VCC Data GND.
  Fan - 4 wire: Fan, 4 wire with tach.
  2-Channel 5v Relay Shield: 2 Channel 5v Relay Shield w. 2x SPD-06VDC-SD-C
